# Fritzing sketch CCC_arduino (1) (saved by Fritzing 0.9.4)
breadboards: 1

parts:
  R2 = Resistor [tolerance=±5% resistance=10k package="2512 [SMD]"]
  TRS1 = Audio Jack (TRS) 3.5mm [package="4Ucon 08780 [THT]"]
  Part5 = Arduino Uno (Rev3) - ICSP
  Part3 = Arduino Uno (Rev3) - ICSP
  U1 = WS2812 RGB LED strip
  J3 = Basic Servo
  Part4 = Arduino Uno (Rev3) - ICSP
  J1 = Infrared Proximity Sensor
  J2 = Basic Force Sensing Resistor (FSR) [package=THT]
  R1 = Resistor [tolerance=±5% resistance=220 package="2010 [SMD]"]
  Part1 = Arduino Uno (Rev3) - ICSP
  Part2 = Arduino Uno (Rev3) - ICSP

nets:
  N1: R2.Pin_0, Part5.GND
  N2: R2.Pin_1, TRS1.Sleeve
  N3: TRS1.Ring, TRS1.Tip, Part5.D8
  GND: Part3.GND, U1.GND
  N4: Part3.D3_PWM, U1.DIN
  5V: Part3.5V, U1.VCC
  GND_2: J3.gnd, Part4.GND
  VCC: J3.vcc, Part4.5V
  N5: J3.pulse, Part4.D9_PWM
  N6: J1.Vout, Part1.A0
  GND_3: J1.GND, Part1.GND
  VCC_2: J1.Vcc, Part1.5V
  N7: J2.pin_0, R1.Pin_1, Part2.A0
  N8: J2.pin_1, Part2.5V
  N9: R1.Pin_0, Part2.GND

custom parts:
  WS2812 RGB LED strip: WS2812 strip

// code stored in the sketch: CCC_arduino_IO.ino

